# Fritzing sketch arduino-nrF24-mega (saved by Fritzing 0.9.2b)
breadboards: 1

parts:
  NRF24L3 = NRF24L01
  R4 = PHOTOCELL [package=photocell-kit]
  T1 = LM35 Temperature Sensor [package="TO92 [THT]"]
  R5 = Resistor [tolerance=±5% resistance=2.2k package="0603 [SMD]"]
  Composant3 = Humidity Sensor - HIH-4030 Breakout
  Composant4 = Arduino Mega 2560 (Rev3)

nets:
  VCC: NRF24L3.VCC, Composant4.3V3
  N1: NRF24L3.CSN, Composant4.D53
  N2: NRF24L3.MOSI, Composant4.D51
  GND: NRF24L3.GND, T1.+Vs, T1.GND, R5.Pin_0, Composant3.GND, Composant4.GND
  N3: NRF24L3.CE, Composant4.D8_PWM
  N4: NRF24L3.SCK, Composant4.D52
  N5: NRF24L3.MISO, Composant4.D50
  VCC_2: R4.P$1, Composant3.VCC, Composant4.5V
  N6: R4.P$2, R5.Pin_1, Composant4.A1
  N7: T1.Vout, Composant4.A0
  N8: Composant3.OUT, Composant4.A2

notes:
  NRF24/Arduino
  GND = GND
  VCC = 3.3V
  CE = D8
  CSN(ss) = D53
  SCK = D52
  MOSI = D51
  MISO = D50
  Temperature: A0
  Lumiere: A1
  Humidité: A2

custom parts:
  NRF24L01: NRF24L01 module
