# Fritzing sketch arduino-nrF24 (saved by Fritzing 0.9.2b)
breadboards: 2

parts:
  NRF24L3 = NRF24L01
  Composant2 = Arduino Nano (Rev3.0)
  R4 = PHOTOCELL [package=photocell-kit]
  T1 = LM35 Temperature Sensor [package="TO92 [THT]"]
  R5 = Resistor [tolerance=±5% resistance=2.2k package="0603 [SMD]"]
  Composant3 = Humidity Sensor - HIH-4030 Breakout

nets:
  VCC: NRF24L3.VCC, Composant2.3V3
  N1: NRF24L3.CSN, Composant2.D7
  N2: NRF24L3.MOSI, Composant2.D11/MOSI
  GND: NRF24L3.GND, Composant2.GND, T1.+Vs, T1.GND, R5.Pin_0, Composant3.GND
  N3: NRF24L3.CE, Composant2.D8
  N4: NRF24L3.SCK, Composant2.D13/SCK
  N5: NRF24L3.MISO, Composant2.D12/MISO
  5V: Composant2.5V, R4.P$1, Composant3.VCC
  N6: Composant2.A2, Composant3.OUT
  N7: Composant2.A1, R4.P$2, R5.Pin_1
  N8: Composant2.A0, T1.Vout

notes:
  NRF24/Arduino
  GND = GND
  VCC = 3.3V
  CE = D8
  CSN(SS) = D7
  SCK = D13
  MOSI = D11
  MISO = D12
  Temperature: A0
  Lumiere: A1
  Humidité: A2

custom parts:
  NRF24L01: NRF24L01 module
